# Fritzing sketch Prueba shift (saved by Fritzing 0.9.3b)
breadboards: 1

parts:
  U1 = L298 [package=multiwatt15]  # not connected
  IC1 = SHIFT REGISTER [package=dil16]
  Part1 = Arduino Uno (Rev3) - ICSP

nets:
  N1: IC1.QB, IC1.QC, Part1.D2
  GND: IC1.GND, Part1.GND
  N2: IC1.QH*, Part1.D3_PWM
  VCC: IC1.SCL, IC1.VCC, Part1.5V
